# Fritzing sketch LeoShifter (saved by Fritzing 0.9.3b)

parts:
  X1 = DB9 Connector [part_number="Not Connected" package=db9]
  Pro_Micro1 = SparkFun Pro Micro

nets:
  N1: X1.1, Pro_Micro1.GND
  N2: X1.2, Pro_Micro1.VCC
  N3: X1.3, Pro_Micro1.A1
  N4: X1.5, Pro_Micro1.9
  N5: X1.6, Pro_Micro1.A0
  N6: X1.7, Pro_Micro1.16
  N7: X1.8, Pro_Micro1.14, Pro_Micro1.RST
  N8: X1.9, Pro_Micro1.15

notes:
  // DB9 Color Description Pro Micro
  // 1 Yellow SCK Button Clock Pin 15
  // 2 Grey MISO Button Data Pin 14
  // 3 Purple CS Button !CS & !PL Pin 16
  // 4 Orange Shifter X axis A0
  // 5 White SPI input (LED Pin) 10
  // 6 Black GND GND
  // 7 Red VCC 5V VCC
  // 8 Green Shifter Y axis A1
  // 9 Not Connected

custom parts:
  SparkFun Pro Micro: The Pro Micro is similar to the Pro Mini except with an ATmega32U4 on board. The USB transceiver inside the 32U4 allows us to add USB connectivity on-board and do away with bulky external USB interface. Based on: https://github.com/unorthodox-engineers/unorthodox-arduino/blob/master/Unorthodox/fritzing/parts/Pro%20Micro.fzpz
